# Fritzing sketch line folower (saved by Fritzing 0.9.4)

parts:
  Part1 = Arduino Uno (Rev3)
  S1 = H-Bridge with L298N
  M1 = DC Motor
  M2 = DC Motor
  M3 = 5-ir-array-sensor [package=THT]
  VCC2 = Battery block 9V
  VCC3 = Battery block 9V
  JP1 = Header 2 [package=r_sw_th]

nets:
  N1: Part1.A1, M3.S1
  N2: Part1.A2, M3.S2
  N3: Part1.A3, M3.S3
  N4: Part1.A4/SDA, M3.S4
  N5: Part1.A5/SCL, M3.S5
  N6: Part1.D9_PWM, S1.ENA
  N7: Part1.D10_PWM/SS, S1.ENB
  N8: Part1.D4, S1.IN1
  N9: Part1.D5_PWM, S1.IN2
  N10: Part1.D6_PWM, S1.IN3
  N11: Part1.D7, S1.IN4
  5V: Part1.5V, M3.VCC
  GND: Part1.GND, M3.GND, VCC3.-
  VIN: Part1.VIN, S1.12V, JP1.1
  N12: S1.GND, VCC2.-
  N13: S1.M1-01, M1.pin_2
  N14: S1.M1-02, M1.pin_1
  N15: S1.M2-01, M2.pin_2
  N16: S1.M2-02, M2.pin_1
  N17: VCC2.+, VCC3.+, JP1.2

custom parts:
  H-Bridge with L298N: h-bridge
  5-ir-array-sensor: 5 IR array sensor.
